# Fritzing sketch arduino circuit (saved by Fritzing 0.9.9b)
breadboards: 1

parts:
  arduino = Arduino Uno (Rev3)
  R1 = Resistor [tolerance=±5% power=0.25 resistance=2k package=THT]
  R2 = Resistor [tolerance=±5% power=0.25 resistance=1k package=THT]
  DHT1 = DHT11 Humitidy and Temperature Sensor
  R3 = Resistor [tolerance=±5% power=0.25 resistance=220 package=THT]
  LED1 = smd LED [color="Red (633nm)" package="0805 [SMD]"]
  R4 = Resistor [tolerance=±5% power=0.25 resistance=220 package=THT]
  LED2 = smd LED [color="Blue (470nm)" package="0805 [SMD]"]
  J1 = Piezo Speaker
  bluetooth_module = Bluetooth HC-05 Macho

nets:
  N1: arduino.D0/RX, bluetooth_module.TXD
  N2: arduino.D1/TX, R2.Pin_1
  N3: arduino.D2, DHT1.DATA
  N4: arduino.D4, R3.Pin_1
  N5: arduino.D5_PWM, R4.Pin_1
  N6: arduino.D6_PWM, J1.pin2
  5V: arduino.5V, DHT1.VDD, bluetooth_module.VCC
  GND: arduino.GND, R1.Pin_0, DHT1.GND, LED1.cathode, LED2.cathode, J1.pin1, bluetooth_module.GND
  N7: R1.Pin_1, R2.Pin_0, bluetooth_module.RXD
  N8: R3.Pin_0, LED1.anode
  N9: R4.Pin_0, LED2.anode

custom parts:
  DHT11 Humitidy and Temperature Sensor: DHT11 Humidity and Temperature Sensor
